# Fritzing sketch Electronics Final Project Fritzing (saved by Fritzing 0.9.1b)
breadboards: 1

parts:
  Part1 = Arduino Uno (Rev3)
  VCC1 = Battery
  S2 = Pushbutton [package="[THT]"]
  J1 = Basic Servo
  J2 = Basic Servo
  J3 = Basic Servo
  J4 = Basic Servo
  R3 = Resistor [tolerance=±5% resistance=220 package=THT]
  LED1 = LED - 5mm [color="Red (633nm)" package="5 mm [THT]"]
  R7 = Resistor [tolerance=±5% resistance=220 package=THT]
  LED2 = LED - 5mm [color="Red (633nm)" package="5 mm [THT]"]
  R8 = Resistor [tolerance=±5% resistance=220 package=THT]
  J5 = Piezo Speaker
  R9 = Rotary Potentiometer (Small) [maximum_resistance=100kΩ package=THT]
  R10 = Resistor [tolerance=±5% resistance=220 package=THT]
  S3 = Pushbutton [package="[THT]"]
  R11 = Resistor [tolerance=±5% resistance=220 package=THT]

nets:
  N1: Part1.A0, R9.wiper
  N2: Part1.A1, S2.Pin_1, S2.Pin_2, R3.Pin_1
  N3: Part1.A2, S3.Pin_1, S3.Pin_2, R11.Pin_1
  N4: Part1.D8, J2.pulse
  N5: Part1.D9_PWM, J1.pulse
  N6: Part1.D10_PWM/SS, J3.pulse
  N7: Part1.D11_PWM/MOSI, J4.pulse
  N8: Part1.D12/MISO, J5.pin2
  GND: Part1.GND, VCC1.-, J1.gnd, J2.gnd, J3.gnd, J4.gnd, R7.Pin_0, R8.Pin_0, J5.pin1, R10.Pin_1
  N9: Part1.D5_PWM, LED1.anode
  N10: Part1.D6_PWM, LED2.anode
  VCC: VCC1.+, S2.Pin_3, S2.Pin_4, J1.vcc, J2.vcc, J3.vcc, J4.vcc, R3.Pin_0, R9.leg1, S3.Pin_3, S3.Pin_4, R11.Pin_0
  N11: LED1.cathode, R7.Pin_1
  N12: LED2.cathode, R8.Pin_1
  N13: R9.leg2, R10.Pin_0
